# Fritzing sketch controller-maze_tilt (saved by Fritzing 1.0.4)
breadboards: 1

parts:
  Composant1 = Adafruit HUZZAH32 ESP32 Feather [part_number="Adafruit #3405"]
  SparkFun_IMU_Breakout_ICM-1 = SparkFun IMU Breakout ICM-20948 [part_number=15335]  # not connected
  R2 = Trimmer Potentiometer [maximum_resistance=10kΩ knob_status=50% power=0.5W package=THT]
  S1 = Pushbutton [package="[THT]"]
  S2 = Pushbutton [package="[THT]"]
  R3 = Resistor [tolerance=±5% power=0.25W resistance=15k package=THT]
  R4 = Resistor [tolerance=±5% power=0.25W resistance=15k package=THT]

nets:
  N1: Composant1.A5_IO4, S1.Pin_3, S1.Pin_4
  N2: Composant1.A3_I39, R2.wiper
  N3: Composant1.A1_DAC1, S2.Pin_3, S2.Pin_4
  N4: Composant1.GND, R2.leg1, S1.Pin_1, S1.Pin_2, S2.Pin_1, S2.Pin_2, R3.Pin_1, R4.Pin_1
  N5: Composant1.3.3V, R2.leg2, R3.Pin_0, R4.Pin_0

notes:
  Emplacement pour batterie LiPo
  L'ESP32 Feather ne possède pas de pull-ups internes pour la communication I²C. Cependant, l'IMU de chez SparkFun en est équipé, il n'est donc pas nécessaire d'en ajouter.
  Alimentation du circuit soit par LiPo via le connecteur JST jack ou via le port micro USB de l'ESP32 Feather

custom parts:
  SparkFun IMU Breakout ICM-20948: The SparkFun 9DoF IMU Breakout incorporates all the amazing features of Invensense's ICM-20948 into a Qwiic-enabled breakout board complete with a logic shifter and broken out GPIO pins for all your motion sensing needs. The ICM-20948 itself is an extremely low powered, I2C and SPI enabled 9-axis motion tracking device that is ideally suited for smartphones, tablets, wearable sensors, and IoT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
